# Fritzing sketch Scheme (saved by Fritzing 0.8.3b)
breadboards: 1

parts:
  AM2303/DHT22 = Humidity and Temperature Sensor RHT03
  Parte1 = Arduino Uno (Rev3)
  R1 = Resistor [tolerance=±5% resistance=100k package=THT]
  R2 = Resistor [tolerance=±5% resistance=120 package=THT]
  R3 = Photocell (LDR) [package=THT]
  LED1-Temperature = LED - 5mm [color="Red (633nm)" package="5 mm [THT]"]
  LED2-Humidity = LED - 5mm [color="Red (633nm)" package="5 mm [THT]"]
  LED3-On/Off = LED - 5mm [color="Red (633nm)" package="5 mm [THT]"]
  R4 = Resistor [tolerance=±5% resistance=100k package=THT]
  R5 = Resistor [tolerance=±5% resistance=100k package=THT]
  LCD1 = LCD screen
  R6 = Rotary Potentiometer (Small)

nets:
  VCC: AM2303/DHT22.Vcc, Parte1.5V, R3.pin_0, LCD1.VDD, LCD1.LED+, R6.leg2
  N1: AM2303/DHT22.Data-signal, Parte1.D9_PWM
  GND: AM2303/DHT22.GND_2, Parte1.GND, R1.Pin_1, R2.Pin_0, R5.Pin_1, LCD1.VSS, LCD1.R/W, LCD1.LED-, R6.leg1
  N2: Parte1.A0, R2.Pin_1, R3.pin_1
  N3: Parte1.D8, LED3-On/Off.anode
  N4: Parte1.D11_PWM/MOSI, LCD1.E
  N5: Parte1.D12/MISO, LCD1.RS
  N6: Parte1.D2, LCD1.DB7
  N7: Parte1.D3_PWM, LCD1.DB6
  N8: Parte1.D4, LCD1.DB5
  N9: Parte1.D5_PWM, LCD1.DB4
  N10: Parte1.D6_PWM, LED1-Temperature.anode
  N11: Parte1.D7, LED2-Humidity.anode
  N12: R1.Pin_0, LED1-Temperature.cathode
  N13: LED2-Humidity.cathode, R4.Pin_0
  N14: LED3-On/Off.cathode, R5.Pin_0
  N15: LCD1.V0, R6.wiper

notes:
  Arduino
  PinA3-LDR
  Pin2-LCD-DB7
  Pin3-LCD-DB6
  Pin4-LCD-DB5
  Pin5-LCD-DB4
  Pin6-LED1-Temp
  Pin7-LED2-Humidity
  Pin8-LED3-On/Off
  Pin-9-DHT22
  Pin10-
  Pin11- LCD-Enable
  Pin12-LCD-RS
  LED's
  LED1-Temperature
  LED2-Humidity
  LED3-On/Off
